// Logisim project BCD_adder.circ as structural Verilog: 4 circuits, main circuit main
module main (
  input  [3:0] A1,
  input  [3:0] B1,
  input  [3:0] A10,
  input  [3:0] B10,
  input  [3:0] A100,
  input  [3:0] B100,
  input  Cin,
  output [3:0] S1,
  output [3:0] S10,
  output [3:0] S100,
  output Cout
);

  wire one_bit_bcd_adder_1_cout, one_bit_bcd_adder_2_cout;

  one_bit_BCD_adder one_bit_bcd_adder_1 (.A(A1), .B(B1), .Cin(Cin), .S(S1), .Cout(one_bit_bcd_adder_1_cout));
  one_bit_BCD_adder one_bit_bcd_adder_2 (
    .A(A10), .B(B10), .Cin(one_bit_bcd_adder_1_cout), .S(S10), .Cout(one_bit_bcd_adder_2_cout));
  one_bit_BCD_adder one_bit_bcd_adder_3 (.A(A100), .B(B100), .Cin(one_bit_bcd_adder_2_cout), .S(S100), .Cout(Cout));
endmodule

module one_bit_BCD_adder (
  input  [3:0] A,
  input  [3:0] B,
  input  Cin,
  output [3:0] S,
  output Cout
);

  wire and_1_out, four_bit_adder_1_cout, or_1_out;
  wire [3:0] four_bit_adder_2_s, S_t;

  four_bit_adder four_bit_adder_1 (.A(A), .B(B), .Cin(Cin), .S(S_t), .Cout(four_bit_adder_1_cout));
  or or_1 (or_1_out, S_t[1], S_t[2]);
  and and_1 (and_1_out, S_t[3], or_1_out);
  or or_2 (Cout, four_bit_adder_1_cout, and_1_out);
  four_bit_adder four_bit_adder_2 (.A(S_t), .B(4'b0110), .Cin(1'b0), .S(four_bit_adder_2_s));  // open: Cout
  Multiplexer #(.width(4)) multiplexer_1 (.in0(S_t), .in1(four_bit_adder_2_s), .out(S), .sel(Cout));
endmodule

module FA (
  input  Cin,
  input  I0,
  input  I1,
  output S,
  output Cout
);

  wire and_1_out, and_2_out, xor_1_out;

  and and_1 (and_1_out, I1, I0);
  xor xor_1 (xor_1_out, I0, I1);
  or or_1 (Cout, and_1_out, and_2_out);
  and and_2 (and_2_out, xor_1_out, Cin);
  xor xor_2 (S, Cin, xor_1_out);
endmodule

module four_bit_adder (
  input  [3:0] A,
  input  [3:0] B,
  input  Cin,
  output [3:0] S,
  output Cout
);

  wire fa_1_cout, fa_2_cout, fa_3_cout;

  FA fa_1 (.Cin(Cin), .I0(A[0]), .I1(B[0]), .S(S[0]), .Cout(fa_1_cout));
  FA fa_2 (.Cin(fa_3_cout), .I0(A[2]), .I1(B[2]), .S(S[2]), .Cout(fa_2_cout));
  FA fa_3 (.Cin(fa_1_cout), .I0(A[1]), .I1(B[1]), .S(S[1]), .Cout(fa_3_cout));
  FA fa_4 (.Cin(fa_2_cout), .I0(A[3]), .I1(B[3]), .S(S[3]), .Cout(Cout));
endmodule
