// Logisim project Floating_Point_Add_Sub.circ as structural Verilog: 6 circuits, main circuit main
module main (
  input  Sub,
  input  [31:0] A,
  input  Clk,
  input  Start,
  input  [31:0] B,
  input  Clr,
  output Done,
  output Overflow,
  output [31:0] C
);

  wire A_Smaller, Align_Done, big_alu_1_carry, normalizer_1_norm_done, Op, Sign_A, Sign_B, Start_Align,
       Start_Norm, xor_1_out;
  wire [7:0] Exp_A, exp_aligner_1_larger_exp, Exp_B;
  wire [23:0] big_alu_1_result, exp_aligner_1_aligned_a, exp_aligner_1_aligned_b, Mant_A, Mant_B;
  wire [23:23] Norm_Frac;
  wire [31:0] register_1_q, register_2_q;

  Register #(.width(32)) register_1 (.D(A), .clk(Clk), .Q(register_1_q), .clr(Clr));  // open: en
  Register #(.width(32)) register_2 (.D(B), .clk(Clk), .Q(register_2_q), .clr(Clr));  // open: en
  xor xor_1 (xor_1_out, Sub, Sign_B);
  Exp_Aligner exp_aligner_1 (
    .Exp_A(Exp_A), .Exp_B(Exp_B), .Mant_A(Mant_A), .Mant_B(Mant_B), .Clk(Clk), .Start_Align(Start_Align),
    .Clr(Clr), .Larger_Exp(exp_aligner_1_larger_exp), .Aligned_A(exp_aligner_1_aligned_a),
    .Aligned_B(exp_aligner_1_aligned_b), .Align_Done(Align_Done), .A_Smaller(A_Smaller));
  Multiplexer multiplexer_1 (.in0(Sign_A), .in1(xor_1_out), .out(C[31]), .sel(A_Smaller));
  Unpacker unpacker_1 (.Inp(register_1_q), .Mantissa(Mant_A), .Exp(Exp_A), .Sign(Sign_A));
  Unpacker unpacker_2 (.Inp(register_2_q), .Mantissa(Mant_B), .Exp(Exp_B), .Sign(Sign_B));
  Big_ALU big_alu_1 (
    .Op(Op), .Frac_A(exp_aligner_1_aligned_a), .Frac_B(exp_aligner_1_aligned_b), .Result(big_alu_1_result),
    .Carry(big_alu_1_carry));
  Normalizer normalizer_1 (
    .ALU_Result(big_alu_1_result), .Larger_Exp(exp_aligner_1_larger_exp), .Carry(big_alu_1_carry), .Clk(Clk),
    .Start_Norm(Start_Norm), .Clr(Clr), .Norm_Exp(C[30:23]), .Norm_Frac({Norm_Frac[23], C[22:0]}),
    .Norm_Done(normalizer_1_norm_done), .Overflow(Overflow));
  ExactlyOne xor_2 (.out(Op), .in0(Sub), .in1(Sign_A), .in2(Sign_B));
  CU cu_1 (
    .Start(Start), .Clk(Clk), .Align_Done(Align_Done), .Norm_Done(normalizer_1_norm_done), .Clr(Clr),
    .Start_Norm(Start_Norm), .Start_Align(Start_Align), .Done(Done));

  // Other names for the same wires on the sheet: Norm_Frac[22:0] = C[22:0]; Result[31:0] = C;
  //   Norm_Exp[7:0] = C[30:23]; Sign_C = C[31]
endmodule

module Unpacker (
  input  [31:0] Inp,
  output [23:0] Mantissa,
  output [7:0] Exp,
  output Sign
);


  assign Exp = Inp[30:23];
  assign Mantissa = {1'b1, Inp[22:0]};
  assign Sign = Inp[31];
endmodule

module Exp_Aligner (
  input  [7:0] Exp_A,
  input  [7:0] Exp_B,
  input  [23:0] Mant_A,
  input  [23:0] Mant_B,
  input  Clk,
  input  Start_Align,
  input  Clr,
  output [7:0] Larger_Exp,
  output [23:0] Aligned_A,
  output [23:0] Aligned_B,
  output Align_Done,
  output A_Smaller
);

  wire Align_Done_Raw, not_1_out, not_2_out, register_2_q;
  wire [7:0] counter_1_q, Smaller_Exp;
  wire [23:0] Aligned_Smaller_Mant, Larger_Mant, multiplexer_7_out, shifter_1_out, Smaller_Mant;

  Comparator #(.mode("unsigned")) comparator_1 (.a(Exp_A), .b(Exp_B), .lt(A_Smaller));  // open: gt, eq
  Multiplexer #(.width(24)) multiplexer_1 (.in0(Mant_A), .in1(Mant_B), .out(Larger_Mant), .sel(A_Smaller));
  Multiplexer #(.width(24)) multiplexer_2 (.in0(Mant_B), .in1(Mant_A), .out(Smaller_Mant), .sel(A_Smaller));
  Multiplexer #(.width(8)) multiplexer_3 (.in0(Exp_A), .in1(Exp_B), .out(Larger_Exp), .sel(A_Smaller));
  Multiplexer #(.width(8)) multiplexer_4 (.in0(Exp_B), .in1(Exp_A), .out(Smaller_Exp), .sel(A_Smaller));
  Multiplexer #(.width(24)) multiplexer_5 (.in0(Mant_A), .in1(Aligned_Smaller_Mant), .out(Aligned_A), .sel(A_Smaller));
  not not_1 (not_1_out, Align_Done);
  Multiplexer #(.width(24)) multiplexer_6 (.in0(Aligned_Smaller_Mant), .in1(Mant_B), .out(Aligned_B), .sel(A_Smaller));
  Counter counter_1 (
    .clr(Clr), .load(Start_Align), .count(not_1_out), .clk(Clk), .D(Smaller_Exp), .Q(counter_1_q));  // open: up, carry
  Multiplexer #(.width(24)) multiplexer_7 (
    .in0(shifter_1_out), .in1(Smaller_Mant), .out(multiplexer_7_out), .sel(Start_Align));
  Register #(.width(24)) register_1 (
    .D(multiplexer_7_out), .en(not_2_out), .clk(Clk), .Q(Aligned_Smaller_Mant), .clr(Clr));
  not not_2 (not_2_out, Align_Done);
  Register #(.width(1)) register_2 (.D(1'b1), .en(Start_Align), .clk(Clk), .Q(register_2_q), .clr(Clr));
  Comparator comparator_2 (.a(counter_1_q), .b(Larger_Exp), .eq(Align_Done_Raw));  // open: gt, lt
  Shifter #(.shift("lr"), .width(24)) shifter_1 (.in(Aligned_Smaller_Mant), .\dist (5'b00001), .out(shifter_1_out));
  and and_1 (Align_Done, register_2_q, Align_Done_Raw);
endmodule

module Big_ALU (
  input  Op,
  input  [23:0] Frac_A,
  input  [23:0] Frac_B,
  output [23:0] Result,
  output Carry
);

  wire A_Smaller, Carry_t, not_1_out;
  wire [23:0] adder_1_out, Max_Frac, Min_Frac, subtractor_1_out;

  Multiplexer #(.width(24)) multiplexer_1 (.in0(Frac_A), .in1(Frac_B), .out(Max_Frac), .sel(A_Smaller));
  Multiplexer #(.width(24)) multiplexer_2 (.in0(Frac_B), .in1(Frac_A), .out(Min_Frac), .sel(A_Smaller));
  Comparator #(.mode("unsigned"), .width(24)) comparator_1 (.a(Frac_A), .b(Frac_B), .lt(A_Smaller));  // open: gt, eq
  and and_1 (Carry, Carry_t, not_1_out);
  not not_1 (not_1_out, Op);
  Adder #(.width(24)) adder_1 (.a(Max_Frac), .b(Min_Frac), .out(adder_1_out), .cout(Carry_t));  // open: cin
  Subtractor #(.width(24)) subtractor_1 (.a(Max_Frac), .b(Min_Frac), .out(subtractor_1_out));  // open: bin, bout
  Multiplexer #(.width(24)) multiplexer_3 (.in0(adder_1_out), .in1(subtractor_1_out), .out(Result), .sel(Op));
endmodule

module Normalizer (
  input  [23:0] ALU_Result,
  input  [7:0] Larger_Exp,
  input  Carry,
  input  Clk,
  input  Start_Norm,
  input  Clr,
  output [7:0] Norm_Exp,
  output [23:0] Norm_Frac,
  output Norm_Done,
  output Overflow
);

  wire comparator_1_eq, Norm_Done_Raw, not_1_out, not_2_out, register_1_q;
  wire [7:0] Exp_Plus, Loading_Exp;
  wire [23:0] Loading_Mant, multiplexer_2_out, shifter_1_out;

  not not_1 (not_1_out, Norm_Done);
  Register #(.width(1)) register_1 (.D(1'b1), .en(Start_Norm), .clk(Clk), .Q(register_1_q), .clr(Clr));
  Multiplexer #(.width(24)) multiplexer_1 (
    .in0(ALU_Result), .in1({1'b1, ALU_Result[23:1]}), .out(Loading_Mant), .sel(Carry));
  Multiplexer #(.width(24)) multiplexer_2 (
    .in0(shifter_1_out), .in1(Loading_Mant), .out(multiplexer_2_out), .sel(Start_Norm));
  Register #(.width(24)) register_2 (.D(multiplexer_2_out), .en(not_1_out), .clk(Clk), .Q(Norm_Frac), .clr(Clr));
  Comparator #(.mode("unsigned"), .width(24)) comparator_1 (
    .a(Norm_Frac), .b({24{1'b0}}), .eq(comparator_1_eq));  // open: gt, lt
  or or_1 (Norm_Done_Raw, Norm_Frac[23], comparator_1_eq);
  and and_1 (Norm_Done, register_1_q, Norm_Done_Raw);
  Shifter #(.width(24)) shifter_1 (.in(Norm_Frac), .\dist (5'b00001), .out(shifter_1_out));
  Multiplexer #(.width(8)) multiplexer_3 (.in0(Larger_Exp), .in1(Exp_Plus), .out(Loading_Exp), .sel(Carry));
  not not_2 (not_2_out, Norm_Done);
  Counter counter_1 (
    .clr(Clr), .load(Start_Norm), .up(1'b0), .count(not_2_out), .clk(Clk), .D(Loading_Exp), .Q(Norm_Exp));  // open: carry
  Adder adder_1 (.a(Larger_Exp), .b(8'h1), .out(Exp_Plus), .cout(Overflow));  // open: cin

  // Other names for the same wires on the sheet: Shift_Right_Frac[22:0] = ALU_Result[23:1]
endmodule

module CU (
  input  Start,
  input  Clk,
  input  Align_Done,
  input  Norm_Done,
  input  Clr,
  output Start_Norm,
  output Start_Align,
  output Done
);

  wire [2:0] Current_State, multiplexer_1_out, multiplexer_2_out, multiplexer_3_out, multiplexer_4_out,
       multiplexer_5_out;

  Multiplexer #(.width(3)) multiplexer_1 (.in0(3'b100), .in1(3'b101), .out(multiplexer_1_out), .sel(Norm_Done));
  Multiplexer #(.width(3)) multiplexer_2 (.in0(3'b101), .in1(3'b001), .out(multiplexer_2_out), .sel(Start));
  Multiplexer #(.width(3)) multiplexer_3 (.in0(3'b000), .in1(3'b001), .out(multiplexer_3_out), .sel(Start));
  Multiplexer #(.width(3)) multiplexer_4 (.in0(3'b010), .in1(3'b011), .out(multiplexer_4_out), .sel(Align_Done));
  Register #(.width(3)) register_1 (.D(multiplexer_5_out), .clk(Clk), .Q(Current_State), .clr(Clr));  // open: en
  Multiplexer #(.select(3), .width(3)) multiplexer_5 (
    .in0(multiplexer_3_out), .in1(3'b010), .in2(multiplexer_4_out), .in3(3'b100), .in4(multiplexer_1_out),
    .in5(multiplexer_2_out), .out(multiplexer_5_out), .sel(Current_State));  // open: in6, in7
  Comparator #(.mode("unsigned"), .width(3)) comparator_1 (
    .a(Current_State), .b(3'b001), .eq(Start_Align));  // open: gt, lt
  Comparator #(.mode("unsigned"), .width(3)) comparator_2 (
    .a(Current_State), .b(3'b011), .eq(Start_Norm));  // open: gt, lt
  Comparator #(.mode("unsigned"), .width(3)) comparator_3 (.a(Current_State), .b(3'b101), .eq(Done));  // open: gt, lt
endmodule
