// Logisim project Data_Memory_and_Jump.circ as structural Verilog: 6 circuits, main circuit main
module main (
  input  Rst,
  input  Clk,
  input  Rst_RAM,
  output [7:0] R0,
  output [7:0] R1,
  output [7:0] R2,
  output [7:0] R3
);

  wire ALU_Inst, C, En_PC, En_Read, En_Write, Jump_Inst, Load_SR, Mem_Inst, O, OE, S, Sub, Write, Z;
  wire [1:0] Dest, J_Condition;
  wire [2:0] Source;
  wire [4:0] Branch_Address, Mem_Address, PC_q;
  wire [7:0] ALU_Out, EPROM_data, IR, ram_1_data, register_1_q;

  Counter #(.max('h1f), .width(5)) PC (
    .clr(Rst), .load(En_PC), .up(1'b1), .clk(Clk), .D(Branch_Address), .Q(PC_q));  // open: count, carry
  RAM #(.addrWidth(5), .asyncread("true"), .databus("bidir")) ram_1 (
    .addr(Mem_Address), .we(En_Write), .oe(En_Read), .clk(Clk), .data(ram_1_data));
  ROM #(.addrWidth(5)) EPROM (.addr(PC_q), .data(EPROM_data));
  CU cu_1 (
    .IR(IR), .C(C), .Z(Z), .S(S), .O(O), .ALU_Inst(ALU_Inst), .J_Condition(J_Condition),
    .Jump_Inst(Jump_Inst), .Write(Write), .Mem_Inst(Mem_Inst), .OE(OE), .En_PC(En_PC), .En_Read(En_Read),
    .En_Write(En_Write), .Load_SR(Load_SR));
  Register register_1 (.D(EPROM_data), .en(1'b1), .clk(Clk), .Q(register_1_q), .clr(Rst));
  assign ram_1_data = OE ? ALU_Out : 8'bz;  // Controlled_Buffer controlled_buffer_1
  Unpacker unpacker_1 (
    .IR(register_1_q), .Source(Source), .Dest(Dest), .Sub(Sub), .ALU_Inst(ALU_Inst),
    .Branch_Address(Branch_Address), .J_Condition(J_Condition), .Jump_Inst(Jump_Inst), .Mem_Inst(Mem_Inst),
    .Mem_Address(Mem_Address), .Write(Write));
  DP dp_1 (
    .Source(Source), .Dest(Dest), .Op(Sub), .Data_In(ram_1_data), .Load_SR(Load_SR), .En_Read(En_Read),
    .Clk(Clk), .Rst(Rst), .ALU_Out(ALU_Out), .R0(R0), .R1(R1), .R2(R2), .R3(R3), .C(C), .Z(Z), .S(S), .O(O));

  // Notes on the sheet:
  //   contents of EPROM (hex, n*v repeats v):
  //   40 c 48 1 70 41 c 49 1 71 42 c 4a 1 72 43 c 4b 1 73 44 c 4c 1 74 45 c 4d 1 75 fe 4
endmodule

module ALU (
  input  [7:0] A,
  input  [7:0] B,
  input  Op,
  output [7:0] Result,
  output C,
  output Z,
  output S,
  output O
);

  wire adder_1_cout, and_1_out, and_2_out, subtractor_1_bout, xnor_1_out, xor_1_out, xor_2_out, xor_3_out;
  wire [7:0] adder_1_out, subtractor_1_out;

  Adder adder_1 (.a(A), .b(B), .out(adder_1_out), .cout(adder_1_cout));  // open: cin
  Subtractor subtractor_1 (.a(A), .b(B), .out(subtractor_1_out), .bout(subtractor_1_bout));  // open: bin
  Multiplexer #(.width(8)) multiplexer_1 (.in0(adder_1_out), .in1(subtractor_1_out), .out(Result), .sel(Op));
  Multiplexer multiplexer_2 (.in0(adder_1_cout), .in1(subtractor_1_bout), .out(C), .sel(Op));
  xor xor_1 (xor_1_out, Result[7], A[7]);
  xnor xnor_1 (xnor_1_out, A[7], B[7]);
  xor xor_2 (xor_2_out, Result[7], A[7]);
  xor xor_3 (xor_3_out, A[7], B[7]);
  and and_1 (and_1_out, xor_1_out, xnor_1_out);
  and and_2 (and_2_out, xor_2_out, xor_3_out);
  nor nor_1 (Z, Result[0], Result[1], Result[2], Result[3], Result[4], Result[5], Result[6], Result[7]);
  Multiplexer multiplexer_3 (.in0(and_1_out), .in1(and_2_out), .out(O), .sel(Op));

  assign S = Result[7];
endmodule

module Reg_File (
  input  Clk,
  input  [1:0] Dest,
  input  [7:0] Data_in,
  input  Enable,
  input  Rst,
  output [7:0] R0,
  output [7:0] R1,
  output [7:0] R2,
  output [7:0] R3
);

  wire decoder_1_out0, decoder_1_out1, decoder_1_out2, decoder_1_out3;

  Decoder #(.select(2)) decoder_1 (
    .out0(decoder_1_out0), .out1(decoder_1_out1), .out2(decoder_1_out2), .out3(decoder_1_out3), .sel(Dest),
    .en(Enable));
  Register register_1 (.D(Data_in), .en(decoder_1_out0), .clk(Clk), .Q(R0), .clr(Rst));
  Register register_2 (.D(Data_in), .en(decoder_1_out1), .clk(Clk), .Q(R1), .clr(Rst));
  Register register_3 (.D(Data_in), .en(decoder_1_out2), .clk(Clk), .Q(R2), .clr(Rst));
  Register register_4 (.D(Data_in), .en(decoder_1_out3), .clk(Clk), .Q(R3), .clr(Rst));
endmodule

module DP (
  input  [2:0] Source,
  input  [1:0] Dest,
  input  Op,
  input  [7:0] Data_In,
  input  Load_SR,
  input  En_Read,
  input  Clk,
  input  Rst,
  output [7:0] ALU_Out,
  output [7:0] R0,
  output [7:0] R1,
  output [7:0] R2,
  output [7:0] R3,
  output C,
  output Z,
  output S,
  output O
);

  wire or_1_out;
  wire [3:0] alu_1_c;
  wire [7:0] B;

  or or_1 (or_1_out, Load_SR, En_Read);
  Reg_File reg_file_1 (
    .Clk(Clk), .Dest(Dest), .Data_in(Data_In), .Enable(or_1_out), .Rst(Rst), .R0(R0), .R1(R1), .R2(R2),
    .R3(R3));
  Multiplexer #(.select(3), .width(8)) multiplexer_1 (
    .in0(R0), .in1(R1), .in2(R2), .in3(R3), .in4({8{1'b0}}), .in5(8'h1), .in6({8{1'b1}}), .out(B),
    .sel(Source));  // open: in7
  ALU alu_1 (.A(R0), .B(B), .Op(Op), .Result(ALU_Out), .C(alu_1_c[0]), .Z(alu_1_c[1]), .S(alu_1_c[2]), .O(alu_1_c[3]));
  Register #(.width(4)) register_1 (.D(alu_1_c), .en(Load_SR), .clk(Clk), .Q({O, S, Z, C}), .clr(Rst));
endmodule

module CU (
  input  [7:0] IR,
  input  C,
  input  Z,
  input  S,
  input  O,
  input  ALU_Inst,
  input  [1:0] J_Condition,
  input  Jump_Inst,
  input  Write,
  input  Mem_Inst,
  output OE,
  output En_PC,
  output En_Read,
  output En_Write,
  output Load_SR
);

  wire multiplexer_1_out, not_1_out, or_1_out;

  Multiplexer #(.select(2)) multiplexer_1 (
    .in0(Z), .in1(S), .in2(O), .in3(1'b1), .out(multiplexer_1_out), .sel(J_Condition));
  and and_1 (En_PC, multiplexer_1_out, Jump_Inst);
  and and_2 (En_Write, Mem_Inst, Write);
  and and_3 (En_Read, Mem_Inst, not_1_out);
  not not_1 (not_1_out, Write);
  or or_1 (or_1_out, En_Write, ALU_Inst);
  not not_2 (OE, En_Read);

  assign Load_SR = ALU_Inst;
endmodule

module Unpacker (
  input  [7:0] IR,
  output [2:0] Source,
  output [1:0] Dest,
  output Sub,
  output ALU_Inst,
  output [4:0] Branch_Address,
  output [1:0] J_Condition,
  output Jump_Inst,
  output Mem_Inst,
  output [4:0] Mem_Address,
  output Write
);

  wire and_3_out, not_1_out, not_2_out, not_3_out;

  Multiplexer #(.width(5)) multiplexer_1 (.in0({5{1'b0}}), .in1(IR[4:0]), .out(Mem_Address), .sel(Mem_Inst));
  and and_1 (Mem_Inst, IR[6], not_1_out);
  not not_1 (not_1_out, IR[7]);
  not not_2 (not_2_out, IR[6]);
  and and_2 (ALU_Inst, not_2_out, not_3_out);
  not not_3 (not_3_out, IR[7]);
  Multiplexer #(.width(2)) multiplexer_2 (.in0(IR[4:3]), .in1(2'b00), .out(Dest), .sel(Mem_Inst));
  and and_3 (and_3_out, Mem_Inst, IR[5]);
  Multiplexer #(.width(3)) multiplexer_3 (.in0(IR[2:0]), .in1(3'b100), .out(Source), .sel(and_3_out));

  assign Branch_Address = IR[4:0];
  assign J_Condition = IR[6:5];
  assign Jump_Inst = IR[7];
  assign Sub = IR[5];
  assign Write = IR[5];

  // Other names for the same wires on the sheet: Mem_Address_IR[4:0] = IR[4:0]; Source_IR[2:0] = IR[2:0];
  //   Dest_IR[1:0] = IR[4:3]; Opcode[1:0] = IR[7:6]
endmodule
