// Logisim project fixed_point_multiplier.circ as structural Verilog: 5 circuits, main circuit main
module main (
  input  [1:0] A_int,
  input  [1:0] A_frac,
  input  Start,
  input  Rst,
  input  [1:0] B_int,
  input  Clk,
  input  [1:0] B_frac,
  output [3:0] C_int,
  output [3:0] C_frac,
  output E
);

  wire clock_1_out, n7486_1_pin4, n7486_1_pin5, n7486_1_pin9, n7486_1_pin10, n7486_1_pin12, n7486_1_pin13,
       n74157_1_pin15, n74283_1_pin2, n74283_1_pin6, n74283_1_pin7, n74283_1_pin11, n74283_1_pin15, not_B0,
       not_B1, not_B2, not_B3, sign;
  wire [3:0] A_unsigend, adder_1_out, B_unsigend, not_1_out, not_2_out;
  wire [7:0] adder_2_out, mul_1_result, not_3_out;

  assign not_1_out = ~{B_int, B_frac};  // NOT_Gate not_1, 4 bits wide
  assign not_2_out = ~{A_int, A_frac};  // NOT_Gate not_2, 4 bits wide
  Adder #(.width(4)) adder_1 (.a(not_2_out), .b(4'b0000), .out(adder_1_out), .cin(1'b1));  // open: cout
  _74283 u_74283_1 (
    .pin1(not_B1), .pin2(n74283_1_pin2), .pin3(not_1_out[1]), .pin4(not_B0), .pin5(not_1_out[0]),
    .pin6(n74283_1_pin6), .pin7(n74283_1_pin7), .pin15(n74283_1_pin15), .pin14(not_1_out[2]), .pin13(not_B2),
    .pin12(not_1_out[3]), .pin11(n74283_1_pin11), .pin10(not_B3));  // open: pin9
  Multiplexer #(.width(4)) multiplexer_1 (.in0({A_int, A_frac}), .in1(adder_1_out), .out(A_unsigend), .sel(A_int[1]));
  _7486 u_7486_1 (
    .pin1(A_int[1]), .pin2(B_int[1]), .pin3(sign), .pin4(n7486_1_pin4), .pin5(n7486_1_pin5),
    .pin13(n7486_1_pin13), .pin12(n7486_1_pin12), .pin10(n7486_1_pin10), .pin9(n7486_1_pin9));  // open: pin6, pin11, pin8
  Clock clock_1 (.out(clock_1_out));
  _74157 u_74157_1 (
    .pin1(B_int[1]), .pin2(B_frac[0]), .pin3(not_B0), .pin4(B_unsigend[0]), .pin5(B_frac[1]), .pin6(not_B1),
    .pin7(B_unsigend[1]), .pin15(n74157_1_pin15), .pin14(B_int[1]), .pin13(not_B3), .pin12(B_unsigend[3]),
    .pin11(B_int[0]), .pin10(not_B2), .pin9(B_unsigend[2]));
  MUL mul_1 (.A(A_unsigend), .B(B_unsigend), .Start(Start), .Rst(Rst), .Clk(clock_1_out), .Result(mul_1_result), .E(E));
  assign not_3_out = ~mul_1_result;  // NOT_Gate not_3, 8 bits wide
  Adder adder_2 (.a(not_3_out), .b({8{1'b0}}), .out(adder_2_out), .cin(1'b1));  // open: cout
  Multiplexer #(.width(8)) multiplexer_2 (.in0(mul_1_result), .in1(adder_2_out), .out({C_int, C_frac}), .sel(sign));
  // also tied to GND on the sheet: {n74283_1_pin15, n74283_1_pin2, n74283_1_pin11, n74283_1_pin6, n7486_1_pin13, n7486_1_pin12, n7486_1_pin4, n7486_1_pin10, n7486_1_pin5, n7486_1_pin9, n74157_1_pin15}
  // also tied to VCC on the sheet: n74283_1_pin7

  // Other names for the same wires on the sheet: A[3:0] = {A_int, A_frac}; B[3:0] = {B_int, B_frac}; B0 = B_frac[0];
  //   B1 = B_frac[1]; B2 = B_int[0]; B3 = B_int[1]
endmodule

module CU (
  input  Clk,
  input  Rst,
  input  Start,
  input  Z,
  output INIT,
  output LOAD,
  output CALC
);

  wire and_1_out, and_2_out, and_4_out, D_CALC, D_INIT, D_LOAD, n7474_1_pin1, n7474_1_pin4, not_2_out,
       not_3_out;

  D_Flip_Flop d_ff_1 (.D(D_INIT), .clk(Clk), .Q(INIT), .preset(Rst));  // open: Qn, reset
  D_Flip_Flop d_ff_2 (.D(D_LOAD), .clk(Clk), .Q(LOAD), .reset(Rst));  // open: Qn, preset
  _7474 u_7474_1 (
    .pin1(n7474_1_pin1), .pin2(D_CALC), .pin3(Clk), .pin4(n7474_1_pin4), .pin5(CALC));  // open: pin6, pin13, pin12, pin11, pin10, pin9, pin8
  not not_1 (n7474_1_pin1, Rst);
  not not_2 (not_2_out, Start);
  and and_1 (and_1_out, CALC, Z);
  not not_3 (not_3_out, Z);
  and and_2 (and_2_out, not_3_out, CALC);
  and and_3 (D_LOAD, INIT, Start);
  and and_4 (and_4_out, INIT, not_2_out);
  or or_1 (D_INIT, and_4_out, and_1_out);
  or or_2 (D_CALC, and_2_out, LOAD);
  // also tied to VCC on the sheet: n7474_1_pin4
endmodule

module SHR (
  input  [7:0] P,
  output [7:0] OUTP
);


  assign OUTP = {1'b0, P[7:1]};
endmodule

module Cnt (
  input  [1:0] D_Count,
  input  dec_Count,
  input  Rst,
  input  ld_Count,
  input  Clk,
  output [1:0] Q_Count
);

  wire or_1_out;
  wire [1:0] adder_1_out, multiplexer_1_out;

  Multiplexer #(.width(2)) multiplexer_1 (.in0(D_Count), .in1(adder_1_out), .out(multiplexer_1_out), .sel(dec_Count));
  or or_1 (or_1_out, dec_Count, ld_Count);
  Register #(.width(2)) register_1 (.D(multiplexer_1_out), .en(or_1_out), .clk(Clk), .Q(Q_Count), .clr(Rst));
  Adder #(.width(2)) adder_1 (.a(Q_Count), .b(2'b11), .out(adder_1_out), .cin(1'b0));  // open: cout
endmodule

module MUL (
  input  [3:0] A,
  input  [3:0] B,
  input  Start,
  input  Rst,
  input  Clk,
  output [7:0] Result,
  output E
);

  wire and_3_out, CALC, INIT, ld_Count, ld_P, n74193_1_pin1, n74193_1_pin2, n74193_1_pin3, n74193_1_pin5,
       n74193_1_pin10, n74193_1_pin11, n74193_1_pin15, n74377_1_pin1, not_1_out, not_2_out, or_2_out, Z;
  wire [1:0] and_2_out;
  wire [3:0] adder_1_out;
  wire [7:0] DP, shr_1_outp;
  wire [7:7] adder_1_cout;

  Adder #(.width(4)) adder_1 (.a(Result[7:4]), .b(A), .out(adder_1_out), .cin(1'b0), .cout(adder_1_cout[7]));
  or or_1 (ld_P, ld_Count, CALC);
  SHR shr_1 (.P(Result), .OUTP(shr_1_outp));
  and and_1 (and_2_out[1], not_1_out, CALC);
  not not_1 (not_1_out, Result[0]);
  Multiplexer #(.select(2), .width(8)) multiplexer_1 (
    .in0({4'b0000, B}), .in1({adder_1_cout[7], adder_1_out, Result[3:1]}), .in2(shr_1_outp), .in3(Result),
    .out(DP), .sel(and_2_out));
  and and_2 (and_2_out[0], CALC, Result[0]);
  not not_2 (not_2_out, CALC);
  Clock #(.phaseOffset(1)) Clk_test ();  // open: out
  or or_2 (or_2_out, not_2_out, Clk);
  _74193 u_74193_1 (
    .pin1(n74193_1_pin1), .pin2(n74193_1_pin2), .pin3(n74193_1_pin3), .pin4(or_2_out), .pin5(n74193_1_pin5),
    .pin15(n74193_1_pin15), .pin14(Rst), .pin11(n74193_1_pin11), .pin10(n74193_1_pin10), .pin9(n74193_1_pin10));  // open: pin6, pin7, pin13, pin12
  Register #(.width(4)) RA (.D(A), .en(ld_Count), .clk(Clk), .clr(Rst));  // open: Q
  not not_3 (n74193_1_pin11, ld_Count);
  _74377 u_74377_1 (
    .pin1(n74377_1_pin1), .pin2(Result[0]), .pin3(DP[0]), .pin4(DP[1]), .pin5(Result[1]), .pin6(Result[2]),
    .pin7(DP[2]), .pin8(DP[3]), .pin9(Result[3]), .pin19(Result[7]), .pin18(DP[7]), .pin17(DP[6]),
    .pin16(Result[6]), .pin15(Result[5]), .pin14(DP[5]), .pin13(DP[4]), .pin12(Result[4]), .pin11(Clk));
  not not_4 (n74377_1_pin1, ld_P);
  nor nor_1 (Z, n74193_1_pin3, n74193_1_pin2);
  CU cu_1 (.Clk(Clk), .Rst(Rst), .Start(Start), .Z(Z), .INIT(INIT), .LOAD(ld_Count), .CALC(CALC));
  and and_3 (and_3_out, Z, CALC);
  S_R_Flip_Flop s_r_ff_1 (.S(and_3_out), .R(Start), .clk(Clk), .Q(E));  // open: reset, Qn, preset
  // also tied to GND on the sheet: n74193_1_pin10
  // also tied to VCC on the sheet: {n74193_1_pin1, n74193_1_pin15, n74193_1_pin5}

  // Other names for the same wires on the sheet: P[7:0] = Result; P0 = Result[0]; ld_RA = ld_Count; LOAD = ld_Count
endmodule
