// Logisim project ALU_Reg_Selection.circ as structural Verilog: 3 circuits, main circuit main
module main (
  input  [5:0] Inst,
  input  Clk,
  input  Clear,
  output [7:0] R0,
  output [7:0] R1,
  output [7:0] R2,
  output [7:0] R3
);

  wire [7:0] A, B, Result;

  Multiplexer #(.select(2), .width(8)) multiplexer_1 (.in0(R0), .in1(R1), .in2(R2), .in3(R3), .out(A), .sel(Inst[4:3]));
  Reg_File reg_file_1 (
    .Clk(Clk), .Dest(Inst[4:3]), .Data_in(Result), .Clear(Clear), .R0(R0), .R1(R1), .R2(R2), .R3(R3));
  Multiplexer #(.select(3), .width(8)) multiplexer_2 (
    .in0(R0), .in1(R1), .in2(R2), .in3(R3), .in4({8{1'b0}}), .in5(8'h1), .in6({8{1'b1}}), .out(B),
    .sel(Inst[2:0]));  // open: in7
  ALU alu_1 (.A(A), .B(B), .Op(Inst[5]), .Result(Result));

  // Other names for the same wires on the sheet: Source[2:0] = Inst[2:0]; Dest[1:0] = Inst[4:3]; Op = Inst[5]
endmodule

module ALU (
  input  [7:0] A,
  input  [7:0] B,
  input  Op,
  output [7:0] Result
);

  wire [7:0] adder_1_out, subtractor_1_out;

  Adder adder_1 (.a(A), .b(B), .out(adder_1_out));  // open: cin, cout
  Subtractor subtractor_1 (.a(A), .b(B), .out(subtractor_1_out));  // open: bin, bout
  Multiplexer #(.width(8)) multiplexer_1 (.in0(adder_1_out), .in1(subtractor_1_out), .out(Result), .sel(Op));
endmodule

module Reg_File (
  input  Clk,
  input  [1:0] Dest,
  input  [7:0] Data_in,
  input  Clear,
  output [7:0] R0,
  output [7:0] R1,
  output [7:0] R2,
  output [7:0] R3
);

  wire decoder_1_out0, decoder_1_out1, decoder_1_out2, decoder_1_out3;

  Decoder #(.select(2)) decoder_1 (
    .out0(decoder_1_out0), .out1(decoder_1_out1), .out2(decoder_1_out2), .out3(decoder_1_out3), .sel(Dest));  // open: en
  Register register_1 (.D(Data_in), .en(decoder_1_out0), .clk(Clk), .Q(R0), .clr(Clear));
  Register register_2 (.D(Data_in), .en(decoder_1_out1), .clk(Clk), .Q(R1), .clr(Clear));
  Register register_3 (.D(Data_in), .en(decoder_1_out2), .clk(Clk), .Q(R2), .clr(Clear));
  Register register_4 (.D(Data_in), .en(decoder_1_out3), .clk(Clk), .Q(R3), .clr(Clear));
endmodule
